// Logisim project 16_bit 1 comp.circ as structural Verilog: 1 circuit, main circuit main
module main (
  input  in_1,
  input  in_2,
  input  [15:0] in_3,
  input  [15:0] in_4,
  input  [2:0] in_5,
  output out_6,
  output out_7,
  output [15:0] out_8
);

  wire [15:0] adder_1_out, and_1_out, nor_1_out, not_1_out, or_1_out, subtractor_1_out, xnor_1_out, xor_1_out;

  Adder #(.width(16)) adder_1 (.a(in_3), .b(in_4), .out(adder_1_out), .cin(in_2), .cout(out_6));
  Subtractor #(.width(16)) subtractor_1 (.a(in_3), .b(in_4), .out(subtractor_1_out), .bin(in_1), .bout(out_7));
  assign not_1_out = ~in_3;  // NOT_Gate not_1, 16 bits wide
  assign nor_1_out = ~(in_3 | in_4);  // NOR_Gate nor_1, 16 bits wide
  assign and_1_out = in_3 & in_4;  // AND_Gate and_1, 16 bits wide
  assign or_1_out = in_3 | in_4;  // OR_Gate or_1, 16 bits wide
  assign xor_1_out = in_3 ^ in_4;  // XOR_Gate xor_1, 16 bits wide
  assign xnor_1_out = ~(in_3 ^ in_4);  // XNOR_Gate xnor_1, 16 bits wide
  Multiplexer #(.select(3), .width(16), .enable("false")) multiplexer_1 (
    .in0(adder_1_out), .in1(subtractor_1_out), .in2(not_1_out), .in3(nor_1_out), .in4(and_1_out),
    .in5(or_1_out), .in6(xor_1_out), .in7(xnor_1_out), .out(out_8), .sel(in_5));
endmodule
