// Logisim project 8bit_alu_sch.circ as structural Verilog: 3 circuits, main circuit main
module main (
  input  in_1,
  input  in_2,
  input  in_3,
  input  [2:0] in_4,
  output out_5,
  output out_6,
  output out_7
);

  wire adder_1_out, and_1_out, nor_1_out, not_1_out, or_1_out, subtractor_1_out, xnor_1_out, xor_1_out;

  Adder #(.width(1)) adder_1 (.a(in_2), .b(in_3), .out(adder_1_out), .cin(in_1), .cout(out_6));
  Subtractor #(.width(1)) subtractor_1 (.a(in_2), .b(in_3), .out(subtractor_1_out), .bin(in_1), .bout(out_5));
  not not_1 (not_1_out, in_2);
  nor nor_1 (nor_1_out, in_2, in_3);
  and and_1 (and_1_out, in_2, in_3);
  or or_1 (or_1_out, in_2, in_3);
  xor xor_1 (xor_1_out, in_2, in_3);
  xnor xnor_1 (xnor_1_out, in_2, in_3);
  Multiplexer #(.select(3), .disabled(0), .enable("false")) multiplexer_1 (
    .in0(adder_1_out), .in1(subtractor_1_out), .in2(not_1_out), .in3(nor_1_out), .in4(and_1_out),
    .in5(or_1_out), .in6(xor_1_out), .in7(xnor_1_out), .out(out_7), .sel(in_4));
endmodule

module eight_bit (
  input  [2:0] opcode,
  input  cin,
  input  [7:0] in_3,
  input  [7:0] B,
  output cout1,
  output [7:0] out_6,
  output cout2
);

  main main_1 (.in_1(cin), .in_2(in_3[0]), .in_3(B[0]), .out_5(cout1), .out_6(cout2), .out_7(out_6[0]), .in_4(opcode));
  main main_2 (.in_1(cin), .in_2(in_3[1]), .in_3(B[1]), .out_5(cout1), .out_6(cout2), .out_7(out_6[0]), .in_4(opcode));
  main main_3 (.in_1(cin), .in_2(in_3[2]), .in_3(B[2]), .out_5(cout1), .out_6(cout2), .out_7(out_6[0]), .in_4(opcode));
  // main main_4: pin names not known; wires that end beside it: in_3[3], B[3], cin, opcode, cout1, out_6, cout2
  main main_5 (.in_1(cin), .in_2(in_3[4]), .in_3(B[4]), .out_5(cout1), .out_6(cout2), .out_7(out_6[0]), .in_4(opcode));
  main main_6 (.in_1(cin), .in_2(in_3[5]), .in_3(B[5]), .out_5(cout1), .out_6(cout2), .out_7(out_6[0]), .in_4(opcode));
  main main_7 (.in_1(cin), .in_2(in_3[7]), .in_3(B[6]), .out_5(cout1), .out_6(cout2), .out_7(out_6[0]), .in_4(opcode));
  main main_8 (.in_1(cin), .in_2(in_3[7]), .in_3(B[7]), .out_5(cout1), .out_6(cout2), .out_7(out_6[0]), .in_4(opcode));
  // Pins of 1 and 8 bits meet at out_6

  assign in_3[6] = in_3[7];

  // Notes on the sheet:
  //   A
endmodule

module _1bit_alu_ic (
);

  main main_1 ();  // open: in_1, in_2, in_3, out_5, out_6, out_7, in_4
endmodule
