// Logisim project onebit_alu_sch.circ as structural Verilog: 2 circuits, main circuit main
module main (
  input  in_1,
  input  in_2,
  input  in_3,
  input  [2:0] in_4,
  output out_5,
  output out_6,
  output out_7
);

  wire adder_1_out, and_1_out, nor_1_out, not_1_out, or_1_out, subtractor_1_out, xnor_1_out, xor_1_out;

  Adder #(.width(1)) adder_1 (.a(in_2), .b(in_3), .out(adder_1_out), .cin(in_1), .cout(out_6));
  Subtractor #(.width(1)) subtractor_1 (.a(in_2), .b(in_3), .out(subtractor_1_out), .bin(in_1), .bout(out_5));
  not not_1 (not_1_out, in_2);
  nor nor_1 (nor_1_out, in_2, in_3);
  and and_1 (and_1_out, in_2, in_3);
  or or_1 (or_1_out, in_2, in_3);
  xor xor_1 (xor_1_out, in_2, in_3);
  xnor xnor_1 (xnor_1_out, in_2, in_3);
  Multiplexer #(.select(3), .disabled(0), .enable("false")) multiplexer_1 (
    .in0(adder_1_out), .in1(subtractor_1_out), .in2(not_1_out), .in3(nor_1_out), .in4(and_1_out),
    .in5(or_1_out), .in6(xor_1_out), .in7(xnor_1_out), .out(out_7), .sel(in_4));
endmodule

module _8bit_alu (
  input  [3:0] cin,
  input  [3:0] B,
  input  [2:0] in_3,
  input  [3:0] A,
  output out_5,
  output out_6,
  output out_7,
  output out_8,
  output [3:0] out_9
);

  main main_1 (.in_1(A[1]), .in_2(B[1]), .in_3(cin[1]), .in_4(in_3), .out_6(out_6), .out_7(out_9[1]));  // open: out_5
  main main_2 (.in_1(A[2]), .in_2(B[2]), .in_3(cin[2]), .in_4(in_3), .out_6(out_8), .out_7(out_9[2]));  // open: out_5
  main main_3 (.in_1(A[3]), .in_2(B[3]), .in_3(cin[3]), .in_4(in_3), .out_6(out_7), .out_7(out_9[3]));  // open: out_5
  main main_4 (.in_1(A[0]), .in_2(B[0]), .in_3(cin[0]), .in_4(in_3), .out_6(out_5), .out_7(out_9[0]));  // open: out_5
endmodule
